# Fritzing sketch 1-button-led (saved by Fritzing 0.9.0b)
breadboards: 1

parts:
  Raspberry_Pi1 = Raspberry Pi B rev2
  LED1 = LED - 5mm [color="Red (633nm)" package="5 mm [THT]"]
  S1 = Pushbutton [package="[THT]"]
  R1 = Resistor [tolerance=±5% resistance=1k package=THT]

nets:
  N1: Raspberry_Pi1.3V3, R1.Pin_0
  N2: Raspberry_Pi1.GND, S1.Pin_3, S1.Pin_4
  N3: Raspberry_Pi1.GPIO_17, LED1.cathode
  N4: Raspberry_Pi1.GPIO_18, S1.Pin_1, S1.Pin_2
  N5: LED1.anode, R1.Pin_1
