# Fritzing sketch 1-led (saved by Fritzing 0.9.0b)
breadboards: 1

parts:
  Raspberry_Pi1 = Raspberry Pi B rev2
  LED1 = LED - 5mm [color="Red (633nm)" package="5 mm [THT]"]
  R1 = Resistor [tolerance=±5% resistance=1k package=THT]

nets:
  N1: Raspberry_Pi1.3V3, R1.Pin_0
  N2: Raspberry_Pi1.GPIO_17, LED1.cathode
  N3: LED1.anode, R1.Pin_1
